// Logisim project projeto-gtn-xtreme.circ as structural Verilog: 8 circuits, main circuit main
module main (
);

  wire button_1_out, clock_1_out, dipswitch_2_p1;
  wire [3:0] dipswitch_1_p1, registrador4_1_q;

  // DipSwitch dipswitch_1: pin names not known; wires that end beside it: dipswitch_1_p1[0], dipswitch_1_p1[1], dipswitch_1_p1[2], dipswitch_1_p1[3]
  Clock clock_1 (.out(clock_1_out));
  // DipSwitch #(.NSwitches(1)) dipswitch_2: pin names not known; wires that end beside it: dipswitch_2_p1
  Registrador4 registrador4_1 (
    .D(dipswitch_1_p1), .Enable(dipswitch_2_p1), .Clock(clock_1_out), .Q(registrador4_1_q),
    .Reset(button_1_out));
  Button button_1 (.out(button_1_out));
  Hex_Digit_Display hex_digit_display_1 (.value(registrador4_1_q));  // open: dp
endmodule

module Registrador4 (
  input  [3:0] D,
  input  Enable,
  input  Clock,
  input  Reset,
  output [3:0] Q
);

  Register #(.width(4), .Select("low")) register_1 (.D(D), .en(Enable), .Q(Q), .clk(Clock), .clr(Reset));
endmodule

module Contador (
  input  Enable,
  input  Clock,
  input  Reset,
  output [3:0] out_4
);

  Counter #(.width(4), .max('h9)) counter_1 (
    .count(Enable), .Q(out_4), .clk(Clock), .clr(Reset), .down(1'b1));  // open: load, D, carry, preset
endmodule

module Somador4b5b (
  input  [3:0] A,
  input  [3:0] B,
  output [4:0] out_3
);

  Adder #(.width(4)) adder_1 (.a(A), .b(B), .out(out_3[3:0]), .cout(out_3[4]));  // open: cin
endmodule

module Comparador_5b (
  input  [4:0] A,
  input  [4:0] B,
  output Igual
);

  Comparator #(.width(5)) comparator_1 (.a(A), .b(B), .eq(Igual));  // open: gt, lt
endmodule

module Diferenca_5b (
  input  [4:0] A,
  input  [4:0] B,
  output [4:0] DIFF
);

  wire SEL;
  wire [4:0] DAB, DBA;

  Multiplexer #(.width(5), .enable("false")) multiplexer_1 (.in0(DAB), .in1(DBA), .out(DIFF), .sel(SEL));
  Subtractor #(.width(5)) subtractor_1 (.a(A), .b(B), .out(DAB), .bin(1'b0), .bout(SEL));
  Subtractor #(.width(5)) subtractor_2 (.a(B), .b(A), .out(DBA), .bin(1'b0));  // open: bout
endmodule

module cores_5b (
  input  [4:0] a,
  output [7:0] out_2,
  output [7:0] out_3
);

  wire [7:0] bit_extender_1_out, shifter_1_out;

  assign bit_extender_1_out = {{3{1'b0}}, a};  // Bit_Extender bit_extender_1
  Shifter shifter_1 (.in(bit_extender_1_out), .\dist (3'b011), .out(shifter_1_out));
  assign out_2 = shifter_1_out | 8'h7;  // OR_Gate or_1, 8 bits wide
  assign out_3 = ~out_2;  // NOT_Gate not_1, 8 bits wide
endmodule

module comparador_4b (
  input  [3:0] A,
  input  [3:0] B,
  output Igual
);

  Comparator #(.width(4)) comparator_1 (.a(A), .b(B), .eq(Igual));  // open: gt, lt
endmodule
